// Logisim project CANNED ICS - copia.circ as structural Verilog: 2 circuits, main circuit main
module main (
  input  in_1,
  input  in_2
);

  wire AJ, and_1_out, and_3_out, and_4_out, and_6_out, and_7_out, and_8_out, AOE, AP, CLK, clock_1_out,
       comparator_1_eq, COUT, d_ff_1_q, d_ff_1_qn, INOE, not_1_out, not_2_out, not_3_out, not_4_out,
       not_7_out, not_8_out, not_10_out, OW, PCW, RAMOE, RAMW, ROMOE;
  wire [3:0] pull_resistor_2_node;
  wire [6:0] keyboard_1_data;
  wire [7:0] adder_1_out, bit_extender_1_out, DATA, register_3_q, register_4_q, register_5_q, register_6_q;
  wire [15:0] ADDRESS, counter_1_q;
  wire [31:0] graphicsadapter_1_out_4, graphicsadapter_1_out_5, graphicsadapter_1_out_6,
       graphicsadapter_1_out_7, graphicsadapter_1_out_8, graphicsadapter_1_out_9, graphicsadapter_1_out_10,
       graphicsadapter_1_out_11, graphicsadapter_1_out_12, graphicsadapter_1_out_13,
       graphicsadapter_1_out_14, graphicsadapter_1_out_15, graphicsadapter_1_out_16,
       graphicsadapter_1_out_17, graphicsadapter_1_out_18, graphicsadapter_1_out_19,
       graphicsadapter_1_out_20, graphicsadapter_1_out_21, graphicsadapter_1_out_22,
       graphicsadapter_1_out_23, graphicsadapter_1_out_24, graphicsadapter_1_out_25,
       graphicsadapter_1_out_26, graphicsadapter_1_out_27, graphicsadapter_1_out_28,
       graphicsadapter_1_out_29, graphicsadapter_1_out_30, graphicsadapter_1_out_31,
       graphicsadapter_1_out_32, graphicsadapter_1_out_33, graphicsadapter_1_out_34, graphicsadapter_1_out_35;

  Clock clock_1 (.out(clock_1_out));
  Register register_1 (.D(ADDRESS[15:8]), .Q(ADDRESS[7:0]), .clk(AP));  // open: en, clr
  Register register_2 (.D(DATA), .Q(ADDRESS[15:8]), .clk(AP));  // open: en, clr
  Register register_3 (.D(DATA), .Q(register_3_q), .clk(AJ));  // open: en, clr
  not not_1 (not_1_out, comparator_1_eq);
  Comparator #(.width(16)) comparator_1 (.a(counter_1_q), .b({16{1'b1}}), .eq(comparator_1_eq));  // open: gt, lt
  and and_1 (and_1_out, ROMOE, CLK);
  Counter #(.width(16), .max('hffff)) counter_1 (
    .load(PCW), .D(ADDRESS), .count(not_2_out), .Q(counter_1_q), .clk(and_1_out), .clr(in_2));  // open: carry
  not not_2 (not_2_out, PCW);
  Register register_4 (.D(adder_1_out), .Q(register_4_q), .clk(AJ));  // open: en, clr
  Adder adder_1 (.a(register_3_q), .b(DATA), .out(adder_1_out), .cin(1'b0), .cout(COUT));
  and and_2 (CLK, clock_1_out, not_1_out);
  assign DATA = AOE ? register_4_q : 8'bz;  // Controlled_Buffer controlled_buffer_1
  ROM #(.addrWidth(16)) rom_1 (.addr(counter_1_q), .data(DATA), .sel(ROMOE));
  RAM #(.addrWidth(16)) ram_1 (.addr(ADDRESS), .data(DATA), .clk(RAMW), .ld(RAMOE));  // open: sel, clr
  // Probe on DATA
  Pull_Resistor pull_resistor_1 (.node(DATA));
  assign DATA = INOE ? bit_extender_1_out : 8'bz;  // Controlled_Buffer controlled_buffer_2
  Pull_Resistor #(.pull(1)) pull_resistor_2 (.node({AJ, AP, RAMW, OW, pull_resistor_2_node}));
  assign {AJ, AP, RAMW, OW, pull_resistor_2_node} = and_4_out ? register_5_q : 8'bz;  // Controlled_Buffer controlled_buffer_3
  Register register_5 (.D(DATA), .Q(register_5_q), .clk(d_ff_1_q));  // open: en, clr
  Register register_6 (.D(DATA), .Q(register_6_q), .clk(OW));  // open: en, clr
  Keyboard keyboard_1 (.clk(register_6_q[0]), .clr(in_1), .data(keyboard_1_data));  // open: re, avail
  not not_3 (not_3_out, AJ);
  D_Flip_Flop d_ff_1 (.clk(CLK), .D(d_ff_1_qn), .Q(d_ff_1_q), .Qn(d_ff_1_qn), .reset(in_2));  // open: preset, en
  not not_4 (not_4_out, CLK);
  // Probe on keyboard_1_data
  and and_3 (and_3_out, not_3_out, COUT);
  and and_4 (and_4_out, d_ff_1_q, not_4_out);
  assign bit_extender_1_out = {{1{1'b0}}, keyboard_1_data};  // Bit_Extender bit_extender_1
  not not_5 (AOE, pull_resistor_2_node[2]);
  not not_6 (RAMOE, pull_resistor_2_node[1]);
  not not_7 (not_7_out, pull_resistor_2_node[3]);
  and and_5 (PCW, RAMW, and_3_out);
  not not_8 (not_8_out, CLK);
  and and_6 (and_6_out, not_8_out, d_ff_1_qn);
  not not_9 (INOE, pull_resistor_2_node[0]);
  or or_1 (ROMOE, not_7_out, and_6_out);
  not not_10 (not_10_out, RAMW);
  and and_7 (and_7_out, not_10_out, and_8_out);
  and and_8 (and_8_out, ADDRESS[8], ADDRESS[9], ADDRESS[10], ADDRESS[11], ADDRESS[12], ADDRESS[13], ADDRESS[14]);
  DotMatrix #(.inputtype("row"), .matrixcols(32), .matrixrows(32), .persist(1)) dotmatrix_1 (
    .row0(graphicsadapter_1_out_4), .row1(graphicsadapter_1_out_8), .row2(graphicsadapter_1_out_12),
    .row3(graphicsadapter_1_out_16), .row4(graphicsadapter_1_out_20), .row5(graphicsadapter_1_out_24),
    .row6(graphicsadapter_1_out_28), .row7(graphicsadapter_1_out_32), .row8(graphicsadapter_1_out_5),
    .row9(graphicsadapter_1_out_9), .row10(graphicsadapter_1_out_13), .row11(graphicsadapter_1_out_17),
    .row12(graphicsadapter_1_out_21), .row13(graphicsadapter_1_out_25), .row14(graphicsadapter_1_out_29),
    .row15(graphicsadapter_1_out_33), .row16(graphicsadapter_1_out_6), .row17(graphicsadapter_1_out_10),
    .row18(graphicsadapter_1_out_14), .row19(graphicsadapter_1_out_18), .row20(graphicsadapter_1_out_22),
    .row21(graphicsadapter_1_out_26), .row22(graphicsadapter_1_out_30), .row23(graphicsadapter_1_out_34),
    .row24(graphicsadapter_1_out_7), .row25(graphicsadapter_1_out_11), .row26(graphicsadapter_1_out_15),
    .row27(graphicsadapter_1_out_19), .row28(graphicsadapter_1_out_23), .row29(graphicsadapter_1_out_27),
    .row30(graphicsadapter_1_out_31), .row31(graphicsadapter_1_out_35));
  GraphicsAdapter graphicsadapter_1 (
    .out_4(graphicsadapter_1_out_4), .VIDEO_ADDRESS(ADDRESS[7:0]), .WRITE(and_7_out),
    .VIDEO_ADDRESS_2(DATA[3:0]), .out_5(graphicsadapter_1_out_5), .out_6(graphicsadapter_1_out_6),
    .out_7(graphicsadapter_1_out_7), .out_8(graphicsadapter_1_out_8), .out_9(graphicsadapter_1_out_9),
    .out_10(graphicsadapter_1_out_10), .out_11(graphicsadapter_1_out_11), .out_12(graphicsadapter_1_out_12),
    .out_13(graphicsadapter_1_out_13), .out_14(graphicsadapter_1_out_14), .out_15(graphicsadapter_1_out_15),
    .out_16(graphicsadapter_1_out_16), .out_17(graphicsadapter_1_out_17), .out_18(graphicsadapter_1_out_18),
    .out_19(graphicsadapter_1_out_19), .out_24(graphicsadapter_1_out_24), .out_25(graphicsadapter_1_out_25),
    .out_26(graphicsadapter_1_out_26), .out_27(graphicsadapter_1_out_27), .out_28(graphicsadapter_1_out_28),
    .out_29(graphicsadapter_1_out_29), .out_30(graphicsadapter_1_out_30), .out_31(graphicsadapter_1_out_31),
    .out_32(graphicsadapter_1_out_32), .out_33(graphicsadapter_1_out_33), .out_34(graphicsadapter_1_out_34),
    .out_35(graphicsadapter_1_out_35), .out_20(graphicsadapter_1_out_20), .out_21(graphicsadapter_1_out_21),
    .out_22(graphicsadapter_1_out_22), .out_23(graphicsadapter_1_out_23));

  // Other names for the same wires on the sheet: RST = in_2

  // Notes on the sheet:
  //   contents of rom_1 (hex, n*v repeats v):
  //   b7 1 bf d7 ff bf df b7 1 3f 7d bf bd b7 1 db 3f 77 ff 7d db 3f 7d b7 23 bf 77 1 bf db b7 7 bf 77 ff
  //   b7 1 bf df bf df b7 1 3f 7d bf bd b7 2 db b7 1 3f 77 80 7d db 3f 77 1 7d db b7 1 3f 7d bf bd b7 2 db
  //   b7 1 3f 77 81 7d db 3f 7d b7 5c bf 77 1 bf db b7 29 bf 77 ff b7 1 bf df bf df b7 1 3f 7d bf bd b7 3
  //   db bf 3f 77 1 7d db b7 1 3f 7d bf bd b7 3 db b7 1 3f 77 1 7d db 3f 7d b7 89 b7 4 77 1 bf bf db b7 62
  //   bf 77 ff bf 3f 7d b7 2 bf 7d bf db 7f 7d b7 a6 bf 77 80 b7 af bf 77 80 bf db b7 1 3f 7d 77 1 db b7 1
  //   3f 7d b7 3 bf 7d b7 1 bf db 7f 7d b7 cb bf 77 80 b7 c bf df b7 d4 bf 77 80 b7 1 bf db b7 c bf d7 1
  //   b7 f 3f 7d b7 e bf bd bb 77 ff 77 ff b7 1 3f 7d 7d db 7f 7d b7 f3 bf 77 80 b7 fc bf 77 80 b7 1 bf db
  //   b7 b bf d7 1 3f 7d 7d db b7 c 3f 7d bf 7d db 7f 7d b7 15 b7 1 77 80 b7 1f b7 1 77 80 bf bf db b7 1
  //   3f 77 1 7d db b7 b 3f 7d b7 c bf db b7 b bf df b7 11 3f 7d b7 10 bf bd bb 77 ff 77 ff bf 3f bd b7 2
  //   7d bf bf db b7 1 3f bd b7 2 7d b7 1 bf db b7 58 b7 1 77 80 b7 61 b7 1 77 80 b7 1 bf db 3f 77 40 7d
  //   db b7 c 3f 7d b7 71 b7 1 77 ff b7 78 b7 1 77 1 b7 1 3f 77 40 7d db bf 3f 7d b7 8b b7 1 77 80 b7 c bf
  //   df b7 93 b7 1 77 80 bf bf db b7 c bf d7 1 b7 13 3f 7d b7 12 bf bd bb 77 ff 77 ff b7 4 bf df b7 5 bf
  //   df b7 6 bf d7 f2 b7 7 bf df b7 d bf df b7 7 3f 7d b7 c bf db bf 3f 7d b7 8 bf db b7 1 3f 7d b7 9 bf
  //   db b7 2 3f 7d bf db b7 3 3f 7d b7 1 bf db b7 12 bf d7 ec b7 13 bf d7 1 b7 38 b7 1 77 ff 77 ff bf 3f
  //   7d b7 2 bf db b7 1 3f 7d b7 3 bf db b7 8 3f 7d bf db b7 9 3f 7d b7 1 bf db b7 c 3f 7d b7 7 bf db b7
  //   c 3f 7d b7 21 b7 2 77 ff b7 97 b7 2 77 1 b7 2 3f 7d b7 8 bf db b7 3 3f 7d b7 9 bf db 3f 7d b7 2 bf
  //   db b7 1 3f 7d b7 3 bf db b7 4 3f 7d bf db b7 5 3f 7d b7 1 bf db b7 e bf d7 5e b7 f bf d7 2 b7 91 bf
  //   77 ff 77 ff bf 3f 7d b7 4 bf db b7 1 3f 7d b7 5 bf db b7 2 3f 7d bf db b7 3 3f 7d b7 1 bf db b7 8 3f
  //   7d b7 2 bf db b7 9 3f 7d b7 3 bf db b7 d 3f 7d b7 b bf 7d b7 d bf db b7 c bf df b7 10 bf d7 ac b7 11
  //   bf d7 2 b7 e1 bf 77 ff 77 ff b7 c 3f 7d b7 b bf db b7 6 3f 7d b7 c8 b7 2 77 1 b7 6 bf db b7 b5 b7 1
  //   77 ff b7 4 3f 7d bf db b7 5 3f 7d b7 1 bf db b7 15 3f 7d b7 14 bf bd bb 77 ff 77 ff bf 3f 7d b7 4 bf
  //   db b7 1 3f 7d b7 5 bf db b7 2 3f 7d b7 6 bf db b7 3 3f 7d b7 7 bf db b7 a bf d7 f2 b7 8 bf df b7 9
  //   bf df b7 4 3f 7d bf db b7 5 3f 7d b7 1 bf db b7 10 bf d7 2e b7 11 bf d7 3 b7 e1 bf 77 ff 77 ff bf 3f
  //   7d b7 4 bf db b7 1 3f 7d b7 5 bf db b7 8 3f 7d bf db b7 9 3f 7d b7 1 bf db b7 10 bf d7 5c b7 11 bf
  //   d7 3 b7 e1 bf 77 ff 77 ff bf 3f 7d b7 8 bf db b7 1 3f 7d b7 9 bf db b7 8 3f 7d bf db b7 9 3f 7d b7 1
  //   bf db b7 6 3f 7d b7 2 bf db b7 7 3f 7d b7 3 bf db bf 3f bd b7 1 77 80 7d bf bf db b7 1 3f bd b7 1 77
  //   80 7d bf db b7 e bf d7 b0 b7 f bf d7 3 b7 91 bf 77 ff 77 ff bf 3f bd b7 1 77 80 7d bf bf db b7 1 3f
  //   bd b7 1 77 80 7d bf db bf 3f 7d b7 8 bf db b7 1 3f 7d b7 9 bf db b7 c 3f 7d b7 e5 b7 3 77 ff b7 23
  //   b7 4 77 1 b7 8 3f 7d bf db b7 9 3f 7d b7 1 bf db b7 6 3f 7d b7 2 bf db b7 7 3f 7d b7 3 bf db b7 e bf
  //   d7 14 b7 f bf d7 4 b7 91 bf 77 ff 77 ff bf 3f 7d b7 8 bf db b7 1 3f 7d b7 9 bf db b7 a 3f 7d b7 37
  //   b7 4 77 1 b7 a bf db b7 f b7 3 77 ff b7 8 3f 7d b7 2 bf db b7 9 3f 7d b7 3 bf db b7 4 3f 7d bf db b7
  //   5 3f 7d b7 1 bf db b7 10 bf d7 66 b7 11 bf d7 4 b7 e1 bf 77 ff 77 ff bf 3f bd b7 1 77 80 7d bf bf db
  //   b7 1 3f bd b7 1 77 80 7d bf db b7 17 3f 7d b7 16 bf bd bb 77 ff 77 ff 7f 77 4 b7 0 bb d7 0 b7 1 bb
  //   d7 0 b7 2 bb d7 0 b7 3 bb d7 0 b7 4 bb d7 0 b7 5 bb d7 2 b7 6 bb d7 2 b7 7 bb d7 2 b7 8 bb d7 0 b7 9
  //   bb d7 2 b7 a bb d7 5 b7 b bb d7 5 b7 c bb d7 0 b7 d bb d7 0 b7 e bb d7 0 b7 f bb d7 0 b7 10 bb d7 0
  //   b7 11 bb d7 5 b7 12 bb d7 f b7 13 bb d7 f b7 14 bb d7 f b7 15 bb d7 f b7 16 bb d7 5 b7 17 bb d7 0 b7
  //   18 bb d7 0 b7 19 bb d7 4 b7 1a bb d7 1 b7 1b bb d7 2 b7 1c bb d7 4 b7 1d bb d7 1 b7 1e bb d7 f b7 1f
  //   bb d7 f b7 20 bb d7 f b7 21 bb d7 f b7 22 bb d7 f b7 23 bb d7 2 b7 24 bb d7 2 b7 25 bb d7 0 b7 26 bb
  //   d7 0 b7 27 bb d7 0 b7 28 bb d7 2 b7 29 bb d7 4 b7 2a bb d7 4 b7 2b bb d7 4 b7 2c bb d7 2 b7 2d bb d7
  //   2 b7 2e bb d7 1 b7 2f bb d7 1 b7 30 bb d7 1 b7 31 bb d7 2 b7 32 bb d7 0 b7 33 bb d7 5 b7 3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
  //   only addition. Good luck.
  //   Read very carefully:
  //   It is utter shit to program on, I'm warning you.
  //   Took me a whole month to have this version of BASIC
  //   working on this machine. I had to debug at a painfully
  //   slow speed of 2 KHz of pure computational power.
  //   You don't multiply or divide long numbers like modern
  //   machines, you better learn to do that because there is
endmodule

module GraphicsAdapter (
  input  [7:0] VIDEO_ADDRESS,
  input  WRITE,
  input  [3:0] VIDEO_ADDRESS_2,
  output [31:0] out_4,
  output [31:0] out_5,
  output [31:0] out_6,
  output [31:0] out_7,
  output [31:0] out_8,
  output [31:0] out_9,
  output [31:0] out_10,
  output [31:0] out_11,
  output [31:0] out_12,
  output [31:0] out_13,
  output [31:0] out_14,
  output [31:0] out_15,
  output [31:0] out_16,
  output [31:0] out_17,
  output [31:0] out_18,
  output [31:0] out_19,
  output [31:0] out_20,
  output [31:0] out_21,
  output [31:0] out_22,
  output [31:0] out_23,
  output [31:0] out_24,
  output [31:0] out_25,
  output [31:0] out_26,
  output [31:0] out_27,
  output [31:0] out_28,
  output [31:0] out_29,
  output [31:0] out_30,
  output [31:0] out_31,
  output [31:0] out_32,
  output [31:0] out_33,
  output [31:0] out_34,
  output [31:0] out_35
);

  wire decoder_1_out0, decoder_1_out1, decoder_1_out2, decoder_1_out3, decoder_1_out4, decoder_1_out5,
       decoder_1_out6, decoder_1_out7, decoder_2_out0, decoder_2_out1, decoder_2_out2, decoder_2_out3,
       decoder_2_out4, decoder_2_out5, decoder_2_out6, decoder_2_out7, decoder_3_out0, decoder_3_out1,
       decoder_3_out2, decoder_3_out3, decoder_3_out4, decoder_3_out5, decoder_3_out6, decoder_3_out7,
       decoder_4_out0, decoder_4_out1, decoder_4_out2, decoder_4_out3, decoder_4_out4, decoder_4_out5,
       decoder_4_out6, decoder_4_out7, decoder_5_out0, decoder_5_out1, decoder_5_out2, decoder_5_out3,
       decoder_5_out4, decoder_5_out5, decoder_5_out6, decoder_5_out7, decoder_6_out0, decoder_6_out1,
       decoder_6_out2, decoder_6_out3, decoder_6_out4, decoder_6_out5, decoder_6_out6, decoder_6_out7,
       decoder_7_out0, decoder_7_out1, decoder_7_out2, decoder_7_out3, decoder_7_out4, decoder_7_out5,
       decoder_7_out6, decoder_7_out7, decoder_8_out0, decoder_8_out1, decoder_8_out2, decoder_8_out3,
       decoder_8_out4, decoder_8_out5, decoder_8_out6, decoder_8_out7, decoder_9_out0, decoder_9_out1,
       decoder_9_out2, decoder_9_out3, decoder_9_out4, decoder_9_out5, decoder_9_out6, decoder_9_out7,
       decoder_10_out0, decoder_10_out1, decoder_10_out2, decoder_10_out3, decoder_10_out4, decoder_10_out5,
       decoder_10_out6, decoder_10_out7, decoder_11_out0, decoder_11_out1, decoder_11_out2, decoder_11_out3,
       decoder_11_out4, decoder_11_out5, decoder_11_out6, decoder_11_out7, decoder_12_out0, decoder_12_out1,
       decoder_12_out2, decoder_12_out3, decoder_12_out4, decoder_12_out5, decoder_12_out6, decoder_12_out7,
       decoder_13_out0, decoder_13_out1, decoder_13_out2, decoder_13_out3, decoder_13_out4, decoder_13_out5,
       decoder_13_out6, decoder_13_out7, decoder_14_out0, decoder_14_out1, decoder_14_out2, decoder_14_out3,
       decoder_14_out4, decoder_14_out5, decoder_14_out6, decoder_14_out7, decoder_15_out0, decoder_15_out1,
       decoder_15_out2, decoder_15_out3, decoder_15_out4, decoder_15_out5, decoder_15_out6, decoder_15_out7,
       decoder_16_out0, decoder_16_out1, decoder_16_out2, decoder_16_out3, decoder_16_out4, decoder_16_out5,
       decoder_16_out6, decoder_16_out7, decoder_17_out0, decoder_17_out1, decoder_17_out2, decoder_17_out3,
       decoder_17_out4, decoder_17_out5, decoder_17_out6, decoder_17_out7, decoder_18_out0, decoder_18_out1,
       decoder_18_out2, decoder_18_out3, decoder_18_out4, decoder_18_out5, decoder_18_out6, decoder_18_out7,
       decoder_19_out0, decoder_19_out1, decoder_19_out2, decoder_19_out3, decoder_19_out4, decoder_19_out5,
       decoder_19_out6, decoder_19_out7, decoder_20_out0, decoder_20_out1, decoder_20_out2, decoder_20_out3,
       decoder_20_out4, decoder_20_out5, decoder_20_out6, decoder_20_out7, decoder_21_out0, decoder_21_out1,
       decoder_21_out2, decoder_21_out3, decoder_21_out4, decoder_21_out5, decoder_21_out6, decoder_21_out7,
       decoder_22_out0, decoder_22_out1, decoder_22_out2, decoder_22_out3, decoder_22_out4, decoder_22_out5,
       decoder_22_out6, decoder_22_out7, decoder_23_out0, decoder_23_out1, decoder_23_out2, decoder_23_out3,
       decoder_23_out4, decoder_23_out5, decoder_23_out6, decoder_23_out7, decoder_24_out0, decoder_24_out1,
       decoder_24_out2, decoder_24_out3, decoder_24_out4, decoder_24_out5, decoder_24_out6, decoder_24_out7,
       decoder_25_out0, decoder_25_out1, decoder_25_out2, decoder_25_out3, decoder_25_out4, decoder_25_out5,
       decoder_25_out6, decoder_25_out7, decoder_26_out0, decoder_26_out1, decoder_26_out2, decoder_26_out3,
       decoder_26_out4, decoder_26_out5, decoder_26_out6, decoder_26_out7, decoder_27_out0, decoder_27_out1,
       decoder_27_out2, decoder_27_out3, decoder_27_out4, decoder_27_out5, decoder_27_out6, decoder_27_out7,
       decoder_28_out0, decoder_28_out1, decoder_28_out2, decoder_28_out3, decoder_28_out4, decoder_28_out5,
       decoder_28_out6, decoder_28_out7, decoder_29_out0, decoder_29_out1, decoder_29_out2, decoder_29_out3,
       decoder_29_out4, decoder_29_out5, decoder_29_out6, decoder_29_out7, decoder_30_out0, decoder_30_out1,
       decoder_30_out2, decoder_30_out3, decoder_30_out4, decoder_30_out5, decoder_30_out6, decoder_30_out7,
       decoder_31_out0, decoder_31_out1, decoder_31_out2, decoder_31_out3, decoder_31_out4, decoder_31_out5,
       decoder_31_out6, decoder_31_out7, decoder_32_out0, decoder_32_out1, decoder_32_out2, decoder_32_out3,
       decoder_32_out4, decoder_32_out5, decoder_32_out6, decoder_32_out7, E0, E1, E2, E3, E4, E5, E6, E7,
       E8, E9, E10, E11, E12, E13, E14, E15, E16, E17, E18, E19, E20, E21, E22, E23, E24, E25, E26, E27, E28,
       E29, E30, E31;

  Decoder #(.select(3), .disabled(0)) decoder_1 (
    .out0(decoder_1_out0), .out1(decoder_1_out1), .out2(decoder_1_out2), .out3(decoder_1_out3),
    .out4(decoder_1_out4), .out5(decoder_1_out5), .out6(decoder_1_out6), .out7(decoder_1_out7),
    .sel(VIDEO_ADDRESS[2:0]), .en(E0));
  Decoder #(.select(3), .disabled(0)) decoder_2 (
    .out0(decoder_2_out0), .out1(decoder_2_out1), .out2(decoder_2_out2), .out3(decoder_2_out3),
    .out4(decoder_2_out4), .out5(decoder_2_out5), .out6(decoder_2_out6), .out7(decoder_2_out7),
    .sel(VIDEO_ADDRESS[2:0]), .en(E1));
  Decoder #(.select(3), .disabled(0)) decoder_3 (
    .out0(decoder_3_out0), .out1(decoder_3_out1), .out2(decoder_3_out2), .out3(decoder_3_out3),
    .out4(decoder_3_out4), .out5(decoder_3_out5), .out6(decoder_3_out6), .out7(decoder_3_out7),
    .sel(VIDEO_ADDRESS[2:0]), .en(E2));
  Decoder #(.select(3), .disabled(0)) decoder_4 (
    .out0(decoder_4_out0), .out1(decoder_4_out1), .out2(decoder_4_out2), .out3(decoder_4_out3),
    .out4(decoder_4_out4), .out5(decoder_4_out5), .out6(decoder_4_out6), .out7(decoder_4_out7),
    .sel(VIDEO_ADDRESS[2:0]), .en(E3));
  Decoder #(.select(3), .disabled(0)) decoder_5 (
    .out0(decoder_5_out0), .out1(decoder_5_out1), .out2(decoder_5_out2), .out3(decoder_5_out3),
    .out4(decoder_5_out4), .out5(decoder_5_out5), .out6(decoder_5_out6), .out7(decoder_5_out7),
    .sel(VIDEO_ADDRESS[2:0]), .en(E4));
  Decoder #(.select(3), .disabled(0)) decoder_6 (
    .out0(decoder_6_out0), .out1(decoder_6_out1), .out2(decoder_6_out2), .out3(decoder_6_out3),
    .out4(decoder_6_out4), .out5(decoder_6_out5), .out6(decoder_6_out6), .out7(decoder_6_out7),
    .sel(VIDEO_ADDRESS[2:0]), .en(E5));
  Decoder #(.select(3), .disabled(0)) decoder_7 (
    .out0(decoder_7_out0), .out1(decoder_7_out1), .out2(decoder_7_out2), .out3(decoder_7_out3),
    .out4(decoder_7_out4), .out5(decoder_7_out5), .out6(decoder_7_out6), .out7(decoder_7_out7),
    .sel(VIDEO_ADDRESS[2:0]), .en(E6));
  Decoder #(.select(3), .disabled(0)) decoder_8 (
    .out0(decoder_8_out0), .out1(decoder_8_out1), .out2(decoder_8_out2), .out3(decoder_8_out3),
    .out4(decoder_8_out4), .out5(decoder_8_out5), .out6(decoder_8_out6), .out7(decoder_8_out7),
    .sel(VIDEO_ADDRESS[2:0]), .en(E7));
  Register #(.width(4)) register_1 (.D(VIDEO_ADDRESS_2), .Q(out_4[3:0]), .clk(decoder_1_out7));  // open: en, clr
  Register #(.width(4)) register_2 (.D(VIDEO_ADDRESS_2), .Q(out_4[7:4]), .clk(decoder_1_out6));  // open: en, clr
  Register #(.width(4)) register_3 (.D(VIDEO_ADDRESS_2), .Q(out_4[11:8]), .clk(decoder_1_out5));  // open: en, clr
  Register #(.width(4)) register_4 (.D(VIDEO_ADDRESS_2), .Q(out_4[15:12]), .clk(decoder_1_out4));  // open: en, clr
  Register #(.width(4)) register_5 (.D(VIDEO_ADDRESS_2), .Q(out_8[3:0]), .clk(decoder_2_out7));  // open: en, clr
  Register #(.width(4)) register_6 (.D(VIDEO_ADDRESS_2), .Q(out_8[7:4]), .clk(decoder_2_out6));  // open: en, clr
  Register #(.width(4)) register_7 (.D(VIDEO_ADDRESS_2), .Q(out_8[11:8]), .clk(decoder_2_out5));  // open: en, clr
  Register #(.width(4)) register_8 (.D(VIDEO_ADDRESS_2), .Q(out_8[15:12]), .clk(decoder_2_out4));  // open: en, clr
  Register #(.width(4)) register_9 (.D(VIDEO_ADDRESS_2), .Q(out_12[3:0]), .clk(decoder_3_out7));  // open: en, clr
  Register #(.width(4)) register_10 (.D(VIDEO_ADDRESS_2), .Q(out_12[7:4]), .clk(decoder_3_out6));  // open: en, clr
  Register #(.width(4)) register_11 (.D(VIDEO_ADDRESS_2), .Q(out_12[11:8]), .clk(decoder_3_out5));  // open: en, clr
  Register #(.width(4)) register_12 (.D(VIDEO_ADDRESS_2), .Q(out_12[15:12]), .clk(decoder_3_out4));  // open: en, clr
  Register #(.width(4)) register_13 (.D(VIDEO_ADDRESS_2), .Q(out_16[3:0]), .clk(decoder_4_out7));  // open: en, clr
  Register #(.width(4)) register_14 (.D(VIDEO_ADDRESS_2), .Q(out_16[7:4]), .clk(decoder_4_out6));  // open: en, clr
  Register #(.width(4)) register_15 (.D(VIDEO_ADDRESS_2), .Q(out_16[11:8]), .clk(decoder_4_out5));  // open: en, clr
  Register #(.width(4)) register_16 (.D(VIDEO_ADDRESS_2), .Q(out_16[15:12]), .clk(decoder_4_out4));  // open: en, clr
  Register #(.width(4)) register_17 (.D(VIDEO_ADDRESS_2), .Q(out_20[3:0]), .clk(decoder_5_out7));  // open: en, clr
  Register #(.width(4)) register_18 (.D(VIDEO_ADDRESS_2), .Q(out_20[7:4]), .clk(decoder_5_out6));  // open: en, clr
  Register #(.width(4)) register_19 (.D(VIDEO_ADDRESS_2), .Q(out_20[11:8]), .clk(decoder_5_out5));  // open: en, clr
  Register #(.width(4)) register_20 (.D(VIDEO_ADDRESS_2), .Q(out_20[15:12]), .clk(decoder_5_out4));  // open: en, clr
  Register #(.width(4)) register_21 (.D(VIDEO_ADDRESS_2), .Q(out_24[3:0]), .clk(decoder_6_out7));  // open: en, clr
  Register #(.width(4)) register_22 (.D(VIDEO_ADDRESS_2), .Q(out_24[7:4]), .clk(decoder_6_out6));  // open: en, clr
  Register #(.width(4)) register_23 (.D(VIDEO_ADDRESS_2), .Q(out_24[11:8]), .clk(decoder_6_out5));  // open: en, clr
  Register #(.width(4)) register_24 (.D(VIDEO_ADDRESS_2), .Q(out_24[15:12]), .clk(decoder_6_out4));  // open: en, clr
  Register #(.width(4)) register_25 (.D(VIDEO_ADDRESS_2), .Q(out_28[3:0]), .clk(decoder_7_out7));  // open: en, clr
  Register #(.width(4)) register_26 (.D(VIDEO_ADDRESS_2), .Q(out_28[7:4]), .clk(decoder_7_out6));  // open: en, clr
  Register #(.width(4)) register_27 (.D(VIDEO_ADDRESS_2), .Q(out_28[11:8]), .clk(decoder_7_out5));  // open: en, clr
  Register #(.width(4)) register_28 (.D(VIDEO_ADDRESS_2), .Q(out_28[15:12]), .clk(decoder_7_out4));  // open: en, clr
  Register #(.width(4)) register_29 (.D(VIDEO_ADDRESS_2), .Q(out_32[3:0]), .clk(decoder_8_out7));  // open: en, clr
  Register #(.width(4)) register_30 (.D(VIDEO_ADDRESS_2), .Q(out_32[7:4]), .clk(decoder_8_out6));  // open: en, clr
  Register #(.width(4)) register_31 (.D(VIDEO_ADDRESS_2), .Q(out_32[11:8]), .clk(decoder_8_out5));  // open: en, clr
  Register #(.width(4)) register_32 (.D(VIDEO_ADDRESS_2), .Q(out_32[15:12]), .clk(decoder_8_out4));  // open: en, clr
  Register #(.width(4)) register_33 (.D(VIDEO_ADDRESS_2), .Q(out_4[19:16]), .clk(decoder_1_out3));  // open: en, clr
  Register #(.width(4)) register_34 (.D(VIDEO_ADDRESS_2), .Q(out_4[23:20]), .clk(decoder_1_out2));  // open: en, clr
  Register #(.width(4)) register_35 (.D(VIDEO_ADDRESS_2), .Q(out_4[27:24]), .clk(decoder_1_out1));  // open: en, clr
  Register #(.width(4)) register_36 (.D(VIDEO_ADDRESS_2), .Q(out_4[31:28]), .clk(decoder_1_out0));  // open: en, clr
  Register #(.width(4)) register_37 (.D(VIDEO_ADDRESS_2), .Q(out_8[19:16]), .clk(decoder_2_out3));  // open: en, clr
  Register #(.width(4)) register_38 (.D(VIDEO_ADDRESS_2), .Q(out_8[23:20]), .clk(decoder_2_out2));  // open: en, clr
  Register #(.width(4)) register_39 (.D(VIDEO_ADDRESS_2), .Q(out_8[27:24]), .clk(decoder_2_out1));  // open: en, clr
  Register #(.width(4)) register_40 (.D(VIDEO_ADDRESS_2), .Q(out_8[31:28]), .clk(decoder_2_out0));  // open: en, clr
  Register #(.width(4)) register_41 (.D(VIDEO_ADDRESS_2), .Q(out_12[19:16]), .clk(decoder_3_out3));  // open: en, clr
  Register #(.width(4)) register_42 (.D(VIDEO_ADDRESS_2), .Q(out_12[23:20]), .clk(decoder_3_out2));  // open: en, clr
  Register #(.width(4)) register_43 (.D(VIDEO_ADDRESS_2), .Q(out_12[27:24]), .clk(decoder_3_out1));  // open: en, clr
  Register #(.width(4)) register_44 (.D(VIDEO_ADDRESS_2), .Q(out_12[31:28]), .clk(decoder_3_out0));  // open: en, clr
  Register #(.width(4)) register_45 (.D(VIDEO_ADDRESS_2), .Q(out_16[19:16]), .clk(decoder_4_out3));  // open: en, clr
  Register #(.width(4)) register_46 (.D(VIDEO_ADDRESS_2), .Q(out_16[23:20]), .clk(decoder_4_out2));  // open: en, clr
  Register #(.width(4)) register_47 (.D(VIDEO_ADDRESS_2), .Q(out_16[27:24]), .clk(decoder_4_out1));  // open: en, clr
  Register #(.width(4)) register_48 (.D(VIDEO_ADDRESS_2), .Q(out_16[31:28]), .clk(decoder_4_out0));  // open: en, clr
  Register #(.width(4)) register_49 (.D(VIDEO_ADDRESS_2), .Q(out_20[19:16]), .clk(decoder_5_out3));  // open: en, clr
  Register #(.width(4)) register_50 (.D(VIDEO_ADDRESS_2), .Q(out_20[23:20]), .clk(decoder_5_out2));  // open: en, clr
  Register #(.width(4)) register_51 (.D(VIDEO_ADDRESS_2), .Q(out_20[27:24]), .clk(decoder_5_out1));  // open: en, clr
  Register #(.width(4)) register_52 (.D(VIDEO_ADDRESS_2), .Q(out_20[31:28]), .clk(decoder_5_out0));  // open: en, clr
  Register #(.width(4)) register_53 (.D(VIDEO_ADDRESS_2), .Q(out_24[19:16]), .clk(decoder_6_out3));  // open: en, clr
  Register #(.width(4)) register_54 (.D(VIDEO_ADDRESS_2), .Q(out_24[23:20]), .clk(decoder_6_out2));  // open: en, clr
  Register #(.width(4)) register_55 (.D(VIDEO_ADDRESS_2), .Q(out_24[27:24]), .clk(decoder_6_out1));  // open: en, clr
  Register #(.width(4)) register_56 (.D(VIDEO_ADDRESS_2), .Q(out_24[31:28]), .clk(decoder_6_out0));  // open: en, clr
  Register #(.width(4)) register_57 (.D(VIDEO_ADDRESS_2), .Q(out_28[19:16]), .clk(decoder_7_out3));  // open: en, clr
  Register #(.width(4)) register_58 (.D(VIDEO_ADDRESS_2), .Q(out_28[23:20]), .clk(decoder_7_out2));  // open: en, clr
  Register #(.width(4)) register_59 (.D(VIDEO_ADDRESS_2), .Q(out_28[27:24]), .clk(decoder_7_out1));  // open: en, clr
  Register #(.width(4)) register_60 (.D(VIDEO_ADDRESS_2), .Q(out_28[31:28]), .clk(decoder_7_out0));  // open: en, clr
  Register #(.width(4)) register_61 (.D(VIDEO_ADDRESS_2), .Q(out_32[19:16]), .clk(decoder_8_out3));  // open: en, clr
  Register #(.width(4)) register_62 (.D(VIDEO_ADDRESS_2), .Q(out_32[23:20]), .clk(decoder_8_out2));  // open: en, clr
  Register #(.width(4)) register_63 (.D(VIDEO_ADDRESS_2), .Q(out_32[27:24]), .clk(decoder_8_out1));  // open: en, clr
  Register #(.width(4)) register_64 (.D(VIDEO_ADDRESS_2), .Q(out_32[31:28]), .clk(decoder_8_out0));  // open: en, clr
  Decoder #(.select(3), .disabled(0)) decoder_9 (
    .out0(decoder_9_out0), .out1(decoder_9_out1), .out2(decoder_9_out2), .out3(decoder_9_out3),
    .out4(decoder_9_out4), .out5(decoder_9_out5), .out6(decoder_9_out6), .out7(decoder_9_out7),
    .sel(VIDEO_ADDRESS[2:0]), .en(E8));
  Decoder #(.select(3), .disabled(0)) decoder_10 (
    .out0(decoder_10_out0), .out1(decoder_10_out1), .out2(decoder_10_out2), .out3(decoder_10_out3),
    .out4(decoder_10_out4), .out5(decoder_10_out5), .out6(decoder_10_out6), .out7(decoder_10_out7),
    .sel(VIDEO_ADDRESS[2:0]), .en(E9));
  Decoder #(.select(3), .disabled(0)) decoder_11 (
    .out0(decoder_11_out0), .out1(decoder_11_out1), .out2(decoder_11_out2), .out3(decoder_11_out3),
    .out4(decoder_11_out4), .out5(decoder_11_out5), .out6(decoder_11_out6), .out7(decoder_11_out7),
    .sel(VIDEO_ADDRESS[2:0]), .en(E10));
  Decoder #(.select(3), .disabled(0)) decoder_12 (
    .out0(decoder_12_out0), .out1(decoder_12_out1), .out2(decoder_12_out2), .out3(decoder_12_out3),
    .out4(decoder_12_out4), .out5(decoder_12_out5), .out6(decoder_12_out6), .out7(decoder_12_out7),
    .sel(VIDEO_ADDRESS[2:0]), .en(E11));
  Decoder #(.select(3), .disabled(0)) decoder_13 (
    .out0(decoder_13_out0), .out1(decoder_13_out1), .out2(decoder_13_out2), .out3(decoder_13_out3),
    .out4(decoder_13_out4), .out5(decoder_13_out5), .out6(decoder_13_out6), .out7(decoder_13_out7),
    .sel(VIDEO_ADDRESS[2:0]), .en(E12));
  Decoder #(.select(3), .disabled(0)) decoder_14 (
    .out0(decoder_14_out0), .out1(decoder_14_out1), .out2(decoder_14_out2), .out3(decoder_14_out3),
    .out4(decoder_14_out4), .out5(decoder_14_out5), .out6(decoder_14_out6), .out7(decoder_14_out7),
    .sel(VIDEO_ADDRESS[2:0]), .en(E13));
  Decoder #(.select(3), .disabled(0)) decoder_15 (
    .out0(decoder_15_out0), .out1(decoder_15_out1), .out2(decoder_15_out2), .out3(decoder_15_out3),
    .out4(decoder_15_out4), .out5(decoder_15_out5), .out6(decoder_15_out6), .out7(decoder_15_out7),
    .sel(VIDEO_ADDRESS[2:0]), .en(E14));
  Decoder #(.select(3), .disabled(0)) decoder_16 (
    .out0(decoder_16_out0), .out1(decoder_16_out1), .out2(decoder_16_out2), .out3(decoder_16_out3),
    .out4(decoder_16_out4), .out5(decoder_16_out5), .out6(decoder_16_out6), .out7(decoder_16_out7),
    .sel(VIDEO_ADDRESS[2:0]), .en(E15));
  Register #(.width(4)) register_65 (.D(VIDEO_ADDRESS_2), .Q(out_5[3:0]), .clk(decoder_9_out7));  // open: en, clr
  Register #(.width(4)) register_66 (.D(VIDEO_ADDRESS_2), .Q(out_5[7:4]), .clk(decoder_9_out6));  // open: en, clr
  Register #(.width(4)) register_67 (.D(VIDEO_ADDRESS_2), .Q(out_5[11:8]), .clk(decoder_9_out5));  // open: en, clr
  Register #(.width(4)) register_68 (.D(VIDEO_ADDRESS_2), .Q(out_5[15:12]), .clk(decoder_9_out4));  // open: en, clr
  Register #(.width(4)) register_69 (.D(VIDEO_ADDRESS_2), .Q(out_9[3:0]), .clk(decoder_10_out7));  // open: en, clr
  Register #(.width(4)) register_70 (.D(VIDEO_ADDRESS_2), .Q(out_9[7:4]), .clk(decoder_10_out6));  // open: en, clr
  Register #(.width(4)) register_71 (.D(VIDEO_ADDRESS_2), .Q(out_9[11:8]), .clk(decoder_10_out5));  // open: en, clr
  Register #(.width(4)) register_72 (.D(VIDEO_ADDRESS_2), .Q(out_9[15:12]), .clk(decoder_10_out4));  // open: en, clr
  Register #(.width(4)) register_73 (.D(VIDEO_ADDRESS_2), .Q(out_13[3:0]), .clk(decoder_11_out7));  // open: en, clr
  Register #(.width(4)) register_74 (.D(VIDEO_ADDRESS_2), .Q(out_13[7:4]), .clk(decoder_11_out6));  // open: en, clr
  Register #(.width(4)) register_75 (.D(VIDEO_ADDRESS_2), .Q(out_13[11:8]), .clk(decoder_11_out5));  // open: en, clr
  Register #(.width(4)) register_76 (.D(VIDEO_ADDRESS_2), .Q(out_13[15:12]), .clk(decoder_11_out4));  // open: en, clr
  Register #(.width(4)) register_77 (.D(VIDEO_ADDRESS_2), .Q(out_17[3:0]), .clk(decoder_12_out7));  // open: en, clr
  Register #(.width(4)) register_78 (.D(VIDEO_ADDRESS_2), .Q(out_17[7:4]), .clk(decoder_12_out6));  // open: en, clr
  Register #(.width(4)) register_79 (.D(VIDEO_ADDRESS_2), .Q(out_17[11:8]), .clk(decoder_12_out5));  // open: en, clr
  Register #(.width(4)) register_80 (.D(VIDEO_ADDRESS_2), .Q(out_17[15:12]), .clk(decoder_12_out4));  // open: en, clr
  Register #(.width(4)) register_81 (.D(VIDEO_ADDRESS_2), .Q(out_21[3:0]), .clk(decoder_13_out7));  // open: en, clr
  Register #(.width(4)) register_82 (.D(VIDEO_ADDRESS_2), .Q(out_21[7:4]), .clk(decoder_13_out6));  // open: en, clr
  Register #(.width(4)) register_83 (.D(VIDEO_ADDRESS_2), .Q(out_21[11:8]), .clk(decoder_13_out5));  // open: en, clr
  Register #(.width(4)) register_84 (.D(VIDEO_ADDRESS_2), .Q(out_21[15:12]), .clk(decoder_13_out4));  // open: en, clr
  Register #(.width(4)) register_85 (.D(VIDEO_ADDRESS_2), .Q(out_25[3:0]), .clk(decoder_14_out7));  // open: en, clr
  Register #(.width(4)) register_86 (.D(VIDEO_ADDRESS_2), .Q(out_25[7:4]), .clk(decoder_14_out6));  // open: en, clr
  Register #(.width(4)) register_87 (.D(VIDEO_ADDRESS_2), .Q(out_25[11:8]), .clk(decoder_14_out5));  // open: en, clr
  Register #(.width(4)) register_88 (.D(VIDEO_ADDRESS_2), .Q(out_25[15:12]), .clk(decoder_14_out4));  // open: en, clr
  Register #(.width(4)) register_89 (.D(VIDEO_ADDRESS_2), .Q(out_29[3:0]), .clk(decoder_15_out7));  // open: en, clr
  Register #(.width(4)) register_90 (.D(VIDEO_ADDRESS_2), .Q(out_29[7:4]), .clk(decoder_15_out6));  // open: en, clr
  Register #(.width(4)) register_91 (.D(VIDEO_ADDRESS_2), .Q(out_29[11:8]), .clk(decoder_15_out5));  // open: en, clr
  Register #(.width(4)) register_92 (.D(VIDEO_ADDRESS_2), .Q(out_29[15:12]), .clk(decoder_15_out4));  // open: en, clr
  Register #(.width(4)) register_93 (.D(VIDEO_ADDRESS_2), .Q(out_33[3:0]), .clk(decoder_16_out7));  // open: en, clr
  Register #(.width(4)) register_94 (.D(VIDEO_ADDRESS_2), .Q(out_33[7:4]), .clk(decoder_16_out6));  // open: en, clr
  Register #(.width(4)) register_95 (.D(VIDEO_ADDRESS_2), .Q(out_33[11:8]), .clk(decoder_16_out5));  // open: en, clr
  Register #(.width(4)) register_96 (.D(VIDEO_ADDRESS_2), .Q(out_33[15:12]), .clk(decoder_16_out4));  // open: en, clr
  Decoder #(.select(3), .disabled(0)) decoder_17 (
    .out0(decoder_17_out0), .out1(decoder_17_out1), .out2(decoder_17_out2), .out3(decoder_17_out3),
    .out4(decoder_17_out4), .out5(decoder_17_out5), .out6(decoder_17_out6), .out7(decoder_17_out7),
    .sel(VIDEO_ADDRESS[2:0]), .en(E16));
  Register #(.width(4)) register_97 (.D(VIDEO_ADDRESS_2), .Q(out_5[19:16]), .clk(decoder_9_out3));  // open: en, clr
  Register #(.width(4)) register_98 (.D(VIDEO_ADDRESS_2), .Q(out_5[23:20]), .clk(decoder_9_out2));  // open: en, clr
  Register #(.width(4)) register_99 (.D(VIDEO_ADDRESS_2), .Q(out_5[27:24]), .clk(decoder_9_out1));  // open: en, clr
  Register #(.width(4)) register_100 (.D(VIDEO_ADDRESS_2), .Q(out_5[31:28]), .clk(decoder_9_out0));  // open: en, clr
  Decoder #(.select(3), .disabled(0)) decoder_18 (
    .out0(decoder_18_out0), .out1(decoder_18_out1), .out2(decoder_18_out2), .out3(decoder_18_out3),
    .out4(decoder_18_out4), .out5(decoder_18_out5), .out6(decoder_18_out6), .out7(decoder_18_out7),
    .sel(VIDEO_ADDRESS[2:0]), .en(E17));
  Register #(.width(4)) register_101 (.D(VIDEO_ADDRESS_2), .Q(out_9[19:16]), .clk(decoder_10_out3));  // open: en, clr
  Register #(.width(4)) register_102 (.D(VIDEO_ADDRESS_2), .Q(out_9[23:20]), .clk(decoder_10_out2));  // open: en, clr
  Register #(.width(4)) register_103 (.D(VIDEO_ADDRESS_2), .Q(out_9[27:24]), .clk(decoder_10_out1));  // open: en, clr
  Register #(.width(4)) register_104 (.D(VIDEO_ADDRESS_2), .Q(out_9[31:28]), .clk(decoder_10_out0));  // open: en, clr
  Decoder #(.select(3), .disabled(0)) decoder_19 (
    .out0(decoder_19_out0), .out1(decoder_19_out1), .out2(decoder_19_out2), .out3(decoder_19_out3),
    .out4(decoder_19_out4), .out5(decoder_19_out5), .out6(decoder_19_out6), .out7(decoder_19_out7),
    .sel(VIDEO_ADDRESS[2:0]), .en(E18));
  Register #(.width(4)) register_105 (.D(VIDEO_ADDRESS_2), .Q(out_13[19:16]), .clk(decoder_11_out3));  // open: en, clr
  Register #(.width(4)) register_106 (.D(VIDEO_ADDRESS_2), .Q(out_13[23:20]), .clk(decoder_11_out2));  // open: en, clr
  Register #(.width(4)) register_107 (.D(VIDEO_ADDRESS_2), .Q(out_13[27:24]), .clk(decoder_11_out1));  // open: en, clr
  Register #(.width(4)) register_108 (.D(VIDEO_ADDRESS_2), .Q(out_13[31:28]), .clk(decoder_11_out0));  // open: en, clr
  Decoder #(.select(3), .disabled(0)) decoder_20 (
    .out0(decoder_20_out0), .out1(decoder_20_out1), .out2(decoder_20_out2), .out3(decoder_20_out3),
    .out4(decoder_20_out4), .out5(decoder_20_out5), .out6(decoder_20_out6), .out7(decoder_20_out7),
    .sel(VIDEO_ADDRESS[2:0]), .en(E19));
  Register #(.width(4)) register_109 (.D(VIDEO_ADDRESS_2), .Q(out_17[19:16]), .clk(decoder_12_out3));  // open: en, clr
  Register #(.width(4)) register_110 (.D(VIDEO_ADDRESS_2), .Q(out_17[23:20]), .clk(decoder_12_out2));  // open: en, clr
  Register #(.width(4)) register_111 (.D(VIDEO_ADDRESS_2), .Q(out_17[27:24]), .clk(decoder_12_out1));  // open: en, clr
  Register #(.width(4)) register_112 (.D(VIDEO_ADDRESS_2), .Q(out_17[31:28]), .clk(decoder_12_out0));  // open: en, clr
  Decoder #(.select(3), .disabled(0)) decoder_21 (
    .out0(decoder_21_out0), .out1(decoder_21_out1), .out2(decoder_21_out2), .out3(decoder_21_out3),
    .out4(decoder_21_out4), .out5(decoder_21_out5), .out6(decoder_21_out6), .out7(decoder_21_out7),
    .sel(VIDEO_ADDRESS[2:0]), .en(E20));
  Register #(.width(4)) register_113 (.D(VIDEO_ADDRESS_2), .Q(out_21[19:16]), .clk(decoder_13_out3));  // open: en, clr
  Register #(.width(4)) register_114 (.D(VIDEO_ADDRESS_2), .Q(out_21[23:20]), .clk(decoder_13_out2));  // open: en, clr
  Register #(.width(4)) register_115 (.D(VIDEO_ADDRESS_2), .Q(out_21[27:24]), .clk(decoder_13_out1));  // open: en, clr
  Register #(.width(4)) register_116 (.D(VIDEO_ADDRESS_2), .Q(out_21[31:28]), .clk(decoder_13_out0));  // open: en, clr
  Decoder #(.select(3), .disabled(0)) decoder_22 (
    .out0(decoder_22_out0), .out1(decoder_22_out1), .out2(decoder_22_out2), .out3(decoder_22_out3),
    .out4(decoder_22_out4), .out5(decoder_22_out5), .out6(decoder_22_out6), .out7(decoder_22_out7),
    .sel(VIDEO_ADDRESS[2:0]), .en(E21));
  Register #(.width(4)) register_117 (.D(VIDEO_ADDRESS_2), .Q(out_25[19:16]), .clk(decoder_14_out3));  // open: en, clr
  Register #(.width(4)) register_118 (.D(VIDEO_ADDRESS_2), .Q(out_25[23:20]), .clk(decoder_14_out2));  // open: en, clr
  Register #(.width(4)) register_119 (.D(VIDEO_ADDRESS_2), .Q(out_25[27:24]), .clk(decoder_14_out1));  // open: en, clr
  Register #(.width(4)) register_120 (.D(VIDEO_ADDRESS_2), .Q(out_25[31:28]), .clk(decoder_14_out0));  // open: en, clr
  Decoder #(.select(3), .disabled(0)) decoder_23 (
    .out0(decoder_23_out0), .out1(decoder_23_out1), .out2(decoder_23_out2), .out3(decoder_23_out3),
    .out4(decoder_23_out4), .out5(decoder_23_out5), .out6(decoder_23_out6), .out7(decoder_23_out7),
    .sel(VIDEO_ADDRESS[2:0]), .en(E22));
  Register #(.width(4)) register_121 (.D(VIDEO_ADDRESS_2), .Q(out_29[19:16]), .clk(decoder_15_out3));  // open: en, clr
  Register #(.width(4)) register_122 (.D(VIDEO_ADDRESS_2), .Q(out_29[23:20]), .clk(decoder_15_out2));  // open: en, clr
  Register #(.width(4)) register_123 (.D(VIDEO_ADDRESS_2), .Q(out_29[27:24]), .clk(decoder_15_out1));  // open: en, clr
  Register #(.width(4)) register_124 (.D(VIDEO_ADDRESS_2), .Q(out_29[31:28]), .clk(decoder_15_out0));  // open: en, clr
  Decoder #(.select(3), .disabled(0)) decoder_24 (
    .out0(decoder_24_out0), .out1(decoder_24_out1), .out2(decoder_24_out2), .out3(decoder_24_out3),
    .out4(decoder_24_out4), .out5(decoder_24_out5), .out6(decoder_24_out6), .out7(decoder_24_out7),
    .sel(VIDEO_ADDRESS[2:0]), .en(E23));
  Register #(.width(4)) register_125 (.D(VIDEO_ADDRESS_2), .Q(out_33[19:16]), .clk(decoder_16_out3));  // open: en, clr
  Register #(.width(4)) register_126 (.D(VIDEO_ADDRESS_2), .Q(out_33[23:20]), .clk(decoder_16_out2));  // open: en, clr
  Register #(.width(4)) register_127 (.D(VIDEO_ADDRESS_2), .Q(out_33[27:24]), .clk(decoder_16_out1));  // open: en, clr
  Register #(.width(4)) register_128 (.D(VIDEO_ADDRESS_2), .Q(out_33[31:28]), .clk(decoder_16_out0));  // open: en, clr
  Register #(.width(4)) register_129 (.D(VIDEO_ADDRESS_2), .Q(out_6[3:0]), .clk(decoder_17_out7));  // open: en, clr
  Register #(.width(4)) register_130 (.D(VIDEO_ADDRESS_2), .Q(out_6[7:4]), .clk(decoder_17_out6));  // open: en, clr
  Register #(.width(4)) register_131 (.D(VIDEO_ADDRESS_2), .Q(out_6[11:8]), .clk(decoder_17_out5));  // open: en, clr
  Register #(.width(4)) register_132 (.D(VIDEO_ADDRESS_2), .Q(out_6[15:12]), .clk(decoder_17_out4));  // open: en, clr
  Register #(.width(4)) register_133 (.D(VIDEO_ADDRESS_2), .Q(out_10[3:0]), .clk(decoder_18_out7));  // open: en, clr
  Register #(.width(4)) register_134 (.D(VIDEO_ADDRESS_2), .Q(out_10[7:4]), .clk(decoder_18_out6));  // open: en, clr
  Register #(.width(4)) register_135 (.D(VIDEO_ADDRESS_2), .Q(out_10[11:8]), .clk(decoder_18_out5));  // open: en, clr
  Register #(.width(4)) register_136 (.D(VIDEO_ADDRESS_2), .Q(out_10[15:12]), .clk(decoder_18_out4));  // open: en, clr
  Register #(.width(4)) register_137 (.D(VIDEO_ADDRESS_2), .Q(out_14[3:0]), .clk(decoder_19_out7));  // open: en, clr
  Register #(.width(4)) register_138 (.D(VIDEO_ADDRESS_2), .Q(out_14[7:4]), .clk(decoder_19_out6));  // open: en, clr
  Register #(.width(4)) register_139 (.D(VIDEO_ADDRESS_2), .Q(out_14[11:8]), .clk(decoder_19_out5));  // open: en, clr
  Register #(.width(4)) register_140 (.D(VIDEO_ADDRESS_2), .Q(out_14[15:12]), .clk(decoder_19_out4));  // open: en, clr
  Register #(.width(4)) register_141 (.D(VIDEO_ADDRESS_2), .Q(out_18[3:0]), .clk(decoder_20_out7));  // open: en, clr
  Register #(.width(4)) register_142 (.D(VIDEO_ADDRESS_2), .Q(out_18[7:4]), .clk(decoder_20_out6));  // open: en, clr
  Register #(.width(4)) register_143 (.D(VIDEO_ADDRESS_2), .Q(out_18[11:8]), .clk(decoder_20_out5));  // open: en, clr
  Register #(.width(4)) register_144 (.D(VIDEO_ADDRESS_2), .Q(out_18[15:12]), .clk(decoder_20_out4));  // open: en, clr
  Register #(.width(4)) register_145 (.D(VIDEO_ADDRESS_2), .Q(out_22[3:0]), .clk(decoder_21_out7));  // open: en, clr
  Register #(.width(4)) register_146 (.D(VIDEO_ADDRESS_2), .Q(out_22[7:4]), .clk(decoder_21_out6));  // open: en, clr
  Register #(.width(4)) register_147 (.D(VIDEO_ADDRESS_2), .Q(out_22[11:8]), .clk(decoder_21_out5));  // open: en, clr
  Register #(.width(4)) register_148 (.D(VIDEO_ADDRESS_2), .Q(out_22[15:12]), .clk(decoder_21_out4));  // open: en, clr
  Register #(.width(4)) register_149 (.D(VIDEO_ADDRESS_2), .Q(out_26[3:0]), .clk(decoder_22_out7));  // open: en, clr
  Register #(.width(4)) register_150 (.D(VIDEO_ADDRESS_2), .Q(out_26[7:4]), .clk(decoder_22_out6));  // open: en, clr
  Register #(.width(4)) register_151 (.D(VIDEO_ADDRESS_2), .Q(out_26[11:8]), .clk(decoder_22_out5));  // open: en, clr
  Register #(.width(4)) register_152 (.D(VIDEO_ADDRESS_2), .Q(out_26[15:12]), .clk(decoder_22_out4));  // open: en, clr
  Register #(.width(4)) register_153 (.D(VIDEO_ADDRESS_2), .Q(out_30[3:0]), .clk(decoder_23_out7));  // open: en, clr
  Register #(.width(4)) register_154 (.D(VIDEO_ADDRESS_2), .Q(out_30[7:4]), .clk(decoder_23_out6));  // open: en, clr
  Register #(.width(4)) register_155 (.D(VIDEO_ADDRESS_2), .Q(out_30[11:8]), .clk(decoder_23_out5));  // open: en, clr
  Register #(.width(4)) register_156 (.D(VIDEO_ADDRESS_2), .Q(out_30[15:12]), .clk(decoder_23_out4));  // open: en, clr
  Register #(.width(4)) register_157 (.D(VIDEO_ADDRESS_2), .Q(out_34[3:0]), .clk(decoder_24_out7));  // open: en, clr
  Register #(.width(4)) register_158 (.D(VIDEO_ADDRESS_2), .Q(out_34[7:4]), .clk(decoder_24_out6));  // open: en, clr
  Register #(.width(4)) register_159 (.D(VIDEO_ADDRESS_2), .Q(out_34[11:8]), .clk(decoder_24_out5));  // open: en, clr
  Register #(.width(4)) register_160 (.D(VIDEO_ADDRESS_2), .Q(out_34[15:12]), .clk(decoder_24_out4));  // open: en, clr
  Register #(.width(4)) register_161 (.D(VIDEO_ADDRESS_2), .Q(out_6[19:16]), .clk(decoder_17_out3));  // open: en, clr
  Register #(.width(4)) register_162 (.D(VIDEO_ADDRESS_2), .Q(out_6[23:20]), .clk(decoder_17_out2));  // open: en, clr
  Register #(.width(4)) register_163 (.D(VIDEO_ADDRESS_2), .Q(out_6[27:24]), .clk(decoder_17_out1));  // open: en, clr
  Register #(.width(4)) register_164 (.D(VIDEO_ADDRESS_2), .Q(out_6[31:28]), .clk(decoder_17_out0));  // open: en, clr
  Register #(.width(4)) register_165 (.D(VIDEO_ADDRESS_2), .Q(out_10[19:16]), .clk(decoder_18_out3));  // open: en, clr
  Register #(.width(4)) register_166 (.D(VIDEO_ADDRESS_2), .Q(out_10[23:20]), .clk(decoder_18_out2));  // open: en, clr
  Register #(.width(4)) register_167 (.D(VIDEO_ADDRESS_2), .Q(out_10[27:24]), .clk(decoder_18_out1));  // open: en, clr
  Register #(.width(4)) register_168 (.D(VIDEO_ADDRESS_2), .Q(out_10[31:28]), .clk(decoder_18_out0));  // open: en, clr
  Register #(.width(4)) register_169 (.D(VIDEO_ADDRESS_2), .Q(out_14[19:16]), .clk(decoder_19_out3));  // open: en, clr
  Register #(.width(4)) register_170 (.D(VIDEO_ADDRESS_2), .Q(out_14[23:20]), .clk(decoder_19_out2));  // open: en, clr
  Register #(.width(4)) register_171 (.D(VIDEO_ADDRESS_2), .Q(out_14[27:24]), .clk(decoder_19_out1));  // open: en, clr
  Register #(.width(4)) register_172 (.D(VIDEO_ADDRESS_2), .Q(out_14[31:28]), .clk(decoder_19_out0));  // open: en, clr
  Register #(.width(4)) register_173 (.D(VIDEO_ADDRESS_2), .Q(out_18[19:16]), .clk(decoder_20_out3));  // open: en, clr
  Register #(.width(4)) register_174 (.D(VIDEO_ADDRESS_2), .Q(out_18[23:20]), .clk(decoder_20_out2));  // open: en, clr
  Register #(.width(4)) register_175 (.D(VIDEO_ADDRESS_2), .Q(out_18[27:24]), .clk(decoder_20_out1));  // open: en, clr
  Register #(.width(4)) register_176 (.D(VIDEO_ADDRESS_2), .Q(out_18[31:28]), .clk(decoder_20_out0));  // open: en, clr
  Register #(.width(4)) register_177 (.D(VIDEO_ADDRESS_2), .Q(out_22[19:16]), .clk(decoder_21_out3));  // open: en, clr
  Register #(.width(4)) register_178 (.D(VIDEO_ADDRESS_2), .Q(out_22[23:20]), .clk(decoder_21_out2));  // open: en, clr
  Register #(.width(4)) register_179 (.D(VIDEO_ADDRESS_2), .Q(out_22[27:24]), .clk(decoder_21_out1));  // open: en, clr
  Register #(.width(4)) register_180 (.D(VIDEO_ADDRESS_2), .Q(out_22[31:28]), .clk(decoder_21_out0));  // open: en, clr
  Register #(.width(4)) register_181 (.D(VIDEO_ADDRESS_2), .Q(out_26[19:16]), .clk(decoder_22_out3));  // open: en, clr
  Register #(.width(4)) register_182 (.D(VIDEO_ADDRESS_2), .Q(out_26[23:20]), .clk(decoder_22_out2));  // open: en, clr
  Register #(.width(4)) register_183 (.D(VIDEO_ADDRESS_2), .Q(out_26[27:24]), .clk(decoder_22_out1));  // open: en, clr
  Register #(.width(4)) register_184 (.D(VIDEO_ADDRESS_2), .Q(out_26[31:28]), .clk(decoder_22_out0));  // open: en, clr
  Register #(.width(4)) register_185 (.D(VIDEO_ADDRESS_2), .Q(out_30[19:16]), .clk(decoder_23_out3));  // open: en, clr
  Register #(.width(4)) register_186 (.D(VIDEO_ADDRESS_2), .Q(out_30[23:20]), .clk(decoder_23_out2));  // open: en, clr
  Register #(.width(4)) register_187 (.D(VIDEO_ADDRESS_2), .Q(out_30[27:24]), .clk(decoder_23_out1));  // open: en, clr
  Register #(.width(4)) register_188 (.D(VIDEO_ADDRESS_2), .Q(out_30[31:28]), .clk(decoder_23_out0));  // open: en, clr
  Register #(.width(4)) register_189 (.D(VIDEO_ADDRESS_2), .Q(out_34[19:16]), .clk(decoder_24_out3));  // open: en, clr
  Register #(.width(4)) register_190 (.D(VIDEO_ADDRESS_2), .Q(out_34[23:20]), .clk(decoder_24_out2));  // open: en, clr
  Register #(.width(4)) register_191 (.D(VIDEO_ADDRESS_2), .Q(out_34[27:24]), .clk(decoder_24_out1));  // open: en, clr
  Register #(.width(4)) register_192 (.D(VIDEO_ADDRESS_2), .Q(out_34[31:28]), .clk(decoder_24_out0));  // open: en, clr
  Decoder #(.select(3), .disabled(0)) decoder_25 (
    .out0(decoder_25_out0), .out1(decoder_25_out1), .out2(decoder_25_out2), .out3(decoder_25_out3),
    .out4(decoder_25_out4), .out5(decoder_25_out5), .out6(decoder_25_out6), .out7(decoder_25_out7),
    .sel(VIDEO_ADDRESS[2:0]), .en(E24));
  Decoder #(.select(3), .disabled(0)) decoder_26 (
    .out0(decoder_26_out0), .out1(decoder_26_out1), .out2(decoder_26_out2), .out3(decoder_26_out3),
    .out4(decoder_26_out4), .out5(decoder_26_out5), .out6(decoder_26_out6), .out7(decoder_26_out7),
    .sel(VIDEO_ADDRESS[2:0]), .en(E25));
  Decoder #(.select(3), .disabled(0)) decoder_27 (
    .out0(decoder_27_out0), .out1(decoder_27_out1), .out2(decoder_27_out2), .out3(decoder_27_out3),
    .out4(decoder_27_out4), .out5(decoder_27_out5), .out6(decoder_27_out6), .out7(decoder_27_out7),
    .sel(VIDEO_ADDRESS[2:0]), .en(E26));
  Decoder #(.select(3), .disabled(0)) decoder_28 (
    .out0(decoder_28_out0), .out1(decoder_28_out1), .out2(decoder_28_out2), .out3(decoder_28_out3),
    .out4(decoder_28_out4), .out5(decoder_28_out5), .out6(decoder_28_out6), .out7(decoder_28_out7),
    .sel(VIDEO_ADDRESS[2:0]), .en(E27));
  Decoder #(.select(3), .disabled(0)) decoder_29 (
    .out0(decoder_29_out0), .out1(decoder_29_out1), .out2(decoder_29_out2), .out3(decoder_29_out3),
    .out4(decoder_29_out4), .out5(decoder_29_out5), .out6(decoder_29_out6), .out7(decoder_29_out7),
    .sel(VIDEO_ADDRESS[2:0]), .en(E28));
  Decoder #(.select(3), .disabled(0)) decoder_30 (
    .out0(decoder_30_out0), .out1(decoder_30_out1), .out2(decoder_30_out2), .out3(decoder_30_out3),
    .out4(decoder_30_out4), .out5(decoder_30_out5), .out6(decoder_30_out6), .out7(decoder_30_out7),
    .sel(VIDEO_ADDRESS[2:0]), .en(E29));
  Decoder #(.select(3), .disabled(0)) decoder_31 (
    .out0(decoder_31_out0), .out1(decoder_31_out1), .out2(decoder_31_out2), .out3(decoder_31_out3),
    .out4(decoder_31_out4), .out5(decoder_31_out5), .out6(decoder_31_out6), .out7(decoder_31_out7),
    .sel(VIDEO_ADDRESS[2:0]), .en(E30));
  Decoder #(.select(3), .disabled(0)) decoder_32 (
    .out0(decoder_32_out0), .out1(decoder_32_out1), .out2(decoder_32_out2), .out3(decoder_32_out3),
    .out4(decoder_32_out4), .out5(decoder_32_out5), .out6(decoder_32_out6), .out7(decoder_32_out7),
    .sel(VIDEO_ADDRESS[2:0]), .en(E31));
  Register #(.width(4)) register_193 (.D(VIDEO_ADDRESS_2), .Q(out_7[3:0]), .clk(decoder_25_out7));  // open: en, clr
  Register #(.width(4)) register_194 (.D(VIDEO_ADDRESS_2), .Q(out_7[7:4]), .clk(decoder_25_out6));  // open: en, clr
  Register #(.width(4)) register_195 (.D(VIDEO_ADDRESS_2), .Q(out_7[11:8]), .clk(decoder_25_out5));  // open: en, clr
  Register #(.width(4)) register_196 (.D(VIDEO_ADDRESS_2), .Q(out_7[15:12]), .clk(decoder_25_out4));  // open: en, clr
  Register #(.width(4)) register_197 (.D(VIDEO_ADDRESS_2), .Q(out_11[3:0]), .clk(decoder_26_out7));  // open: en, clr
  Register #(.width(4)) register_198 (.D(VIDEO_ADDRESS_2), .Q(out_11[7:4]), .clk(decoder_26_out6));  // open: en, clr
  Register #(.width(4)) register_199 (.D(VIDEO_ADDRESS_2), .Q(out_11[11:8]), .clk(decoder_26_out5));  // open: en, clr
  Register #(.width(4)) register_200 (.D(VIDEO_ADDRESS_2), .Q(out_11[15:12]), .clk(decoder_26_out4));  // open: en, clr
  Register #(.width(4)) register_201 (.D(VIDEO_ADDRESS_2), .Q(out_15[3:0]), .clk(decoder_27_out7));  // open: en, clr
  Register #(.width(4)) register_202 (.D(VIDEO_ADDRESS_2), .Q(out_15[7:4]), .clk(decoder_27_out6));  // open: en, clr
  Register #(.width(4)) register_203 (.D(VIDEO_ADDRESS_2), .Q(out_15[11:8]), .clk(decoder_27_out5));  // open: en, clr
  Register #(.width(4)) register_204 (.D(VIDEO_ADDRESS_2), .Q(out_15[15:12]), .clk(decoder_27_out4));  // open: en, clr
  Register #(.width(4)) register_205 (.D(VIDEO_ADDRESS_2), .Q(out_19[3:0]), .clk(decoder_28_out7));  // open: en, clr
  Register #(.width(4)) register_206 (.D(VIDEO_ADDRESS_2), .Q(out_19[7:4]), .clk(decoder_28_out6));  // open: en, clr
  Register #(.width(4)) register_207 (.D(VIDEO_ADDRESS_2), .Q(out_19[11:8]), .clk(decoder_28_out5));  // open: en, clr
  Register #(.width(4)) register_208 (.D(VIDEO_ADDRESS_2), .Q(out_19[15:12]), .clk(decoder_28_out4));  // open: en, clr
  Register #(.width(4)) register_209 (.D(VIDEO_ADDRESS_2), .Q(out_23[3:0]), .clk(decoder_29_out7));  // open: en, clr
  Register #(.width(4)) register_210 (.D(VIDEO_ADDRESS_2), .Q(out_23[7:4]), .clk(decoder_29_out6));  // open: en, clr
  Register #(.width(4)) register_211 (.D(VIDEO_ADDRESS_2), .Q(out_23[11:8]), .clk(decoder_29_out5));  // open: en, clr
  Register #(.width(4)) register_212 (.D(VIDEO_ADDRESS_2), .Q(out_23[15:12]), .clk(decoder_29_out4));  // open: en, clr
  Register #(.width(4)) register_213 (.D(VIDEO_ADDRESS_2), .Q(out_27[3:0]), .clk(decoder_30_out7));  // open: en, clr
  Register #(.width(4)) register_214 (.D(VIDEO_ADDRESS_2), .Q(out_27[7:4]), .clk(decoder_30_out6));  // open: en, clr
  Register #(.width(4)) register_215 (.D(VIDEO_ADDRESS_2), .Q(out_27[11:8]), .clk(decoder_30_out5));  // open: en, clr
  Register #(.width(4)) register_216 (.D(VIDEO_ADDRESS_2), .Q(out_27[15:12]), .clk(decoder_30_out4));  // open: en, clr
  Register #(.width(4)) register_217 (.D(VIDEO_ADDRESS_2), .Q(out_31[3:0]), .clk(decoder_31_out7));  // open: en, clr
  Register #(.width(4)) register_218 (.D(VIDEO_ADDRESS_2), .Q(out_31[7:4]), .clk(decoder_31_out6));  // open: en, clr
  Register #(.width(4)) register_219 (.D(VIDEO_ADDRESS_2), .Q(out_31[11:8]), .clk(decoder_31_out5));  // open: en, clr
  Register #(.width(4)) register_220 (.D(VIDEO_ADDRESS_2), .Q(out_31[15:12]), .clk(decoder_31_out4));  // open: en, clr
  Register #(.width(4)) register_221 (.D(VIDEO_ADDRESS_2), .Q(out_35[3:0]), .clk(decoder_32_out7));  // open: en, clr
  Register #(.width(4)) register_222 (.D(VIDEO_ADDRESS_2), .Q(out_35[7:4]), .clk(decoder_32_out6));  // open: en, clr
  Register #(.width(4)) register_223 (.D(VIDEO_ADDRESS_2), .Q(out_35[11:8]), .clk(decoder_32_out5));  // open: en, clr
  Register #(.width(4)) register_224 (.D(VIDEO_ADDRESS_2), .Q(out_35[15:12]), .clk(decoder_32_out4));  // open: en, clr
  Register #(.width(4)) register_225 (.D(VIDEO_ADDRESS_2), .Q(out_7[19:16]), .clk(decoder_25_out3));  // open: en, clr
  Register #(.width(4)) register_226 (.D(VIDEO_ADDRESS_2), .Q(out_7[23:20]), .clk(decoder_25_out2));  // open: en, clr
  Register #(.width(4)) register_227 (.D(VIDEO_ADDRESS_2), .Q(out_7[27:24]), .clk(decoder_25_out1));  // open: en, clr
  Register #(.width(4)) register_228 (.D(VIDEO_ADDRESS_2), .Q(out_7[31:28]), .clk(decoder_25_out0));  // open: en, clr
  Register #(.width(4)) register_229 (.D(VIDEO_ADDRESS_2), .Q(out_11[19:16]), .clk(decoder_26_out3));  // open: en, clr
  Register #(.width(4)) register_230 (.D(VIDEO_ADDRESS_2), .Q(out_11[23:20]), .clk(decoder_26_out2));  // open: en, clr
  Register #(.width(4)) register_231 (.D(VIDEO_ADDRESS_2), .Q(out_11[27:24]), .clk(decoder_26_out1));  // open: en, clr
  Register #(.width(4)) register_232 (.D(VIDEO_ADDRESS_2), .Q(out_11[31:28]), .clk(decoder_26_out0));  // open: en, clr
  Register #(.width(4)) register_233 (.D(VIDEO_ADDRESS_2), .Q(out_15[19:16]), .clk(decoder_27_out3));  // open: en, clr
  Register #(.width(4)) register_234 (.D(VIDEO_ADDRESS_2), .Q(out_15[23:20]), .clk(decoder_27_out2));  // open: en, clr
  Register #(.width(4)) register_235 (.D(VIDEO_ADDRESS_2), .Q(out_15[27:24]), .clk(decoder_27_out1));  // open: en, clr
  Register #(.width(4)) register_236 (.D(VIDEO_ADDRESS_2), .Q(out_15[31:28]), .clk(decoder_27_out0));  // open: en, clr
  Register #(.width(4)) register_237 (.D(VIDEO_ADDRESS_2), .Q(out_19[19:16]), .clk(decoder_28_out3));  // open: en, clr
  Register #(.width(4)) register_238 (.D(VIDEO_ADDRESS_2), .Q(out_19[23:20]), .clk(decoder_28_out2));  // open: en, clr
  Register #(.width(4)) register_239 (.D(VIDEO_ADDRESS_2), .Q(out_19[27:24]), .clk(decoder_28_out1));  // open: en, clr
  Register #(.width(4)) register_240 (.D(VIDEO_ADDRESS_2), .Q(out_19[31:28]), .clk(decoder_28_out0));  // open: en, clr
  Register #(.width(4)) register_241 (.D(VIDEO_ADDRESS_2), .Q(out_23[19:16]), .clk(decoder_29_out3));  // open: en, clr
  Register #(.width(4)) register_242 (.D(VIDEO_ADDRESS_2), .Q(out_23[23:20]), .clk(decoder_29_out2));  // open: en, clr
  Register #(.width(4)) register_243 (.D(VIDEO_ADDRESS_2), .Q(out_23[27:24]), .clk(decoder_29_out1));  // open: en, clr
  Register #(.width(4)) register_244 (.D(VIDEO_ADDRESS_2), .Q(out_23[31:28]), .clk(decoder_29_out0));  // open: en, clr
  Register #(.width(4)) register_245 (.D(VIDEO_ADDRESS_2), .Q(out_27[19:16]), .clk(decoder_30_out3));  // open: en, clr
  Register #(.width(4)) register_246 (.D(VIDEO_ADDRESS_2), .Q(out_27[23:20]), .clk(decoder_30_out2));  // open: en, clr
  Register #(.width(4)) register_247 (.D(VIDEO_ADDRESS_2), .Q(out_27[27:24]), .clk(decoder_30_out1));  // open: en, clr
  Register #(.width(4)) register_248 (.D(VIDEO_ADDRESS_2), .Q(out_27[31:28]), .clk(decoder_30_out0));  // open: en, clr
  Register #(.width(4)) register_249 (.D(VIDEO_ADDRESS_2), .Q(out_31[19:16]), .clk(decoder_31_out3));  // open: en, clr
  Register #(.width(4)) register_250 (.D(VIDEO_ADDRESS_2), .Q(out_31[23:20]), .clk(decoder_31_out2));  // open: en, clr
  Register #(.width(4)) register_251 (.D(VIDEO_ADDRESS_2), .Q(out_31[27:24]), .clk(decoder_31_out1));  // open: en, clr
  Register #(.width(4)) register_252 (.D(VIDEO_ADDRESS_2), .Q(out_31[31:28]), .clk(decoder_31_out0));  // open: en, clr
  Register #(.width(4)) register_253 (.D(VIDEO_ADDRESS_2), .Q(out_35[19:16]), .clk(decoder_32_out3));  // open: en, clr
  Register #(.width(4)) register_254 (.D(VIDEO_ADDRESS_2), .Q(out_35[23:20]), .clk(decoder_32_out2));  // open: en, clr
  Register #(.width(4)) register_255 (.D(VIDEO_ADDRESS_2), .Q(out_35[27:24]), .clk(decoder_32_out1));  // open: en, clr
  Register #(.width(4)) register_256 (.D(VIDEO_ADDRESS_2), .Q(out_35[31:28]), .clk(decoder_32_out0));  // open: en, clr
  Decoder #(.select(5), .disabled(0)) decoder_33 (
    .out0(E0), .out1(E1), .out2(E2), .out3(E3), .out4(E4), .out5(E5), .out6(E6), .out7(E7), .out8(E8),
    .out9(E9), .out10(E10), .out11(E11), .out12(E12), .out13(E13), .out14(E14), .out15(E15), .out16(E16),
    .out17(E17), .out18(E18), .out19(E19), .out20(E20), .out21(E21), .out22(E22), .out23(E23), .out24(E24),
    .out25(E25), .out26(E26), .out27(E27), .out28(E28), .out29(E29), .out30(E30), .out31(E31),
    .sel(VIDEO_ADDRESS[7:3]), .en(WRITE));

  // Other names for the same wires on the sheet: ADDR[2:0] = VIDEO_ADDRESS[2:0]; DATAIN[3:0] = VIDEO_ADDRESS_2
endmodule
